# Fritzing sketch diagrama_conexion (saved by Fritzing 0.9.4)

parts:
  U1 = ESP32-38PinWide [part_number=ESP32-38PinWide]
  OLED1 = OLED 128x64 I2C Monochrome Display
  J1 = Piezo Speaker
  J2 = Piezo Speaker

nets:
  N1: U1.3.3, OLED1.VDD
  N2: U1.GPIO25, J1.pin2
  N3: U1.GPIO26, J2.pin2
  N4: U1.GPIO11, J2.pin1
  N5: U1.GPIO21, OLED1.SDA
  N6: U1.GPIO22, OLED1.SCK
  GND: U1.GND, OLED1.GND

custom parts:
  ESP32-38PinWide: Generic 38-Pin ESP32 with wide format (only access to one side of pins on a breadboard) based on Stephen Lilley's HiLetgo ESP-WROOM-32 ESP32 ESP-32S Development Board.
